# Fritzing sketch Wether_Station (saved by Fritzing 0.9.2b)
circuit board: 8.46667cm x 5.64444cm
breadboards: 1

parts:
  Part2 = Arduino Nano (Rev3.0) (ICSP)
  OLED1 = 128x64 Monochrom OLED Display with SPI Control
  PART1 = ML8511 UV Sensor Breakout [part_number=SEN-12705]
  DS1 = DS18B20 1-Wire Temperature Sensor [part_number=DS18B20]
  R1 = Resistor [tolerance=±5% resistance=4.7 package="0603 [SMD]"]

nets:
  GND: Part2.GND, OLED1.GND, PART1.GND, DS1.GND
  N1: Part2.D2, DS1.DQ, R1.Pin_0
  N2: Part2.D8, OLED1.Reset
  N3: Part2.D10, OLED1.CS
  N4: Part2.D11/MOSI, OLED1.Data
  5V: Part2.5V, DS1.VDD, R1.Pin_1
  3V3: Part2.A1, Part2.3V3, OLED1.3v3, PART1.EN, PART1.3.3V
  N5: Part2.A0, PART1.OUT

custom parts:
  ML8511 UV Sensor Breakout: Description: The ML8511 breakout is an easy to use ultraviolet light sensor. The MP8511 UV Sensor works by outputing an analog signal in relation to the amount of UV light it detects. This breakout can be very handy in creating devices that warn the user of sunburn or detect the UV index as it relates to weather conditions. This sensor breakout can detect 280-390nm light most effectively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
